# Fritzing sketch circuitDiagram (saved by Fritzing 0.9.3b)

parts:
  Part1 = Arduino Mega 2560 (Rev3)
  J1 = Basic Servo
  S1 = Pushbutton [package="[SMD]"]
  S2 = Pushbutton [package="[SMD]"]
  S3 = Pushbutton [package="[SMD]"]
  R2 = Resistor [tolerance=±5% resistance=10k package="2512 [SMD]"]
  R1 = Resistor [tolerance=±5% resistance=10k package="2512 [SMD]"]
  R3 = Resistor [tolerance=±5% resistance=10k package="2512 [SMD]"]
  sen136b5b1 = sen136b5b

nets:
  N1: Part1.D18/TX1, S2.Pin_1, S2.Pin_2, R3.Pin_0
  GND: Part1.GND, J1.gnd, R2.Pin_1, R1.Pin_1, R3.Pin_1, sen136b5b1.Gnd
  N2: Part1.D13_PWM, sen136b5b1.VCC
  5V: Part1.5V, J1.vcc
  N3: Part1.D2_PWM, S3.Pin_1, S3.Pin_2, R2.Pin_0
  N4: Part1.D3_PWM, S1.Pin_1, S1.Pin_2, R1.Pin_0
  N5: Part1.D4_PWM, S1.Pin_4, S2.Pin_3, S2.Pin_4, S3.Pin_3, S3.Pin_4
  N6: Part1.D6_PWM, J1.pulse
  N7: Part1.D7_PWM, sen136b5b1.sig

custom parts:
  sen136b5b: This is a sen136b5b Distance Sensor
